# Fritzing sketch mhz19c_pwm_mega (saved by Fritzing 0.9.10b)
breadboards: 1

parts:
  Grove1 = Grove OLED 128x96
  MH-Z19C1 = MH-Z19C
  Bauteil1 = Arduino Mega ADK (Rev3)

nets:
  GND: Grove1.GND, MH-Z19C1.GND, Bauteil1.GND
  VCC: Grove1.VCC, MH-Z19C1.Vin, Bauteil1.IOREF, Bauteil1.5V
  N1: Grove1.SDA, Bauteil1.D20/SDA
  N2: Grove1.SCL, Bauteil1.D21/SCL
  N3: MH-Z19C1.PWM, Bauteil1.D3_PWM

custom parts:
  MH-Z19C: CO2-Sensor https://www.winsen-sensor.com/
